# Fritzing sketch buzzer (saved by Fritzing 0.9.3b)
breadboards: 1

parts:
  LED1 = 7-SEGMENT-4DIGIT-YOUNGSUN [package=7-segment-4digit-youngsun]
  J1 = Piezo Speaker
  S1 = Pushbutton [package="[THT]"]
  LED3 = LED - 5mm [color="Red (633nm)" package="5 mm [THT]"]
  LED10 = LED - 5mm [color="Red (633nm)" package="5 mm [THT]"]
  LED19 = LED - 5mm [color="Red (633nm)" package="5 mm [THT]"]
  LED21 = LED - 5mm [color="Red (633nm)" package="5 mm [THT]"]
  LED23 = LED - 5mm [color="Red (633nm)" package="5 mm [THT]"]
  LED24 = LED - 5mm [color="Red (633nm)" package="5 mm [THT]"]
  LED25 = LED - 5mm [color="Red (633nm)" package="5 mm [THT]"]
  Mod1 = Raspberry Pi Pico
  R1 = Resistor [tolerance=±5% resistance=220 package="0603 [SMD]"]
  R2 = Resistor [tolerance=±5% resistance=220 package="0603 [SMD]"]
  R3 = Resistor [tolerance=±5% resistance=220 package="0603 [SMD]"]
  R4 = Resistor [tolerance=±5% resistance=220 package="0603 [SMD]"]
  R5 = Resistor [tolerance=±5% resistance=220 package="0603 [SMD]"]
  R6 = Resistor [tolerance=±5% resistance=220 package="0603 [SMD]"]
  R7 = Resistor [tolerance=±5% resistance=220 package="0603 [SMD]"]
  Q1 = PNP-Transistor [package="TO92 [THT]"]
  R8 = Resistor [tolerance=±5% resistance=220 package="0603 [SMD]"]

nets:
  N1: LED1.DIG1, Mod1.pin_4, R4.Pin_1
  N2: LED1.DIG2, Mod1.pin_5, R3.Pin_1
  N3: LED1.D, Mod1.pin_11
  N4: LED1.E, Mod1.pin_12
  N5: LED1.DIG3, Mod1.pin_6, R1.Pin_1
  N6: LED1.DP, Mod1.pin_15
  N7: LED1.DIG4, Mod1.pin_7, R2.Pin_1
  GND: LED1.F, LED1.A, S1.Pin_1, S1.Pin_2, LED3.cathode, LED10.cathode, LED19.cathode, LED21.cathode, LED23.cathode, LED24.cathode, LED25.cathode, Mod1.pin_8, Mod1.pin_13, Mod1.pin_38, Mod1.pin_42, R5.Pin_1, Q1.C
  N8: LED1.C, Mod1.pin_10, R7.Pin_1
  N9: LED1.G, Mod1.pin_14
  N10: LED1.B, Mod1.pin_9, R6.Pin_1
  N11: J1.pin1, Q1.E
  N12: J1.pin2, S1.Pin_4, Mod1.pin_39
  N13: LED3.anode, R1.Pin_0
  N14: LED10.anode, R3.Pin_0
  N15: LED19.anode, R4.Pin_0
  N16: LED21.anode, R2.Pin_0
  N17: LED23.anode, R7.Pin_0
  N18: LED24.anode, R5.Pin_0
  N19: LED25.anode, R6.Pin_0
  N20: Mod1.pin_34, R8.Pin_0
  N21: Q1.B, R8.Pin_1

custom parts:
  Raspberry Pi Pico: Raspberry Pi Pico. Based around the RP2040 microcontroller the Pico is a low cost microcontroller device bringing Raspberry Pi quality, cost, and easy of use to the microcontroller space. Jan 2021, Split part in to two versions: tht (this one) and SMD. This one will drill holes for a .1 in header in pcb to allow plugging in the module as well as providing pads to solder the module to the top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
