# Fritzing sketch ekran (saved by Fritzing 0.9.3b)
breadboards: 1

parts:
  Mod1 = Raspberry Pi Pico
  Part1 = TFT 2.8 inch 320x240 Touch w microSD [part_number=1770]
  RE2 = KY-040 Rotary encoder [package=THT]

nets:
  N1: Mod1.pin_17, RE2.SW
  N2: Mod1.pin_19, RE2.DT
  N3: Mod1.pin_20, RE2.CLK
  N4: Mod1.pin_21, Part1.MISO
  N5: Mod1.pin_22, Part1.LCD_CS
  N6: Mod1.pin_24, Part1.SCLK
  N7: Mod1.pin_25, Part1.MOSI
  N8: Mod1.pin_26, Part1.LCD_DC
  N9: Mod1.pin_27, Part1.LCD_RST
  GND: Mod1.pin_33, Mod1.pin_38, Part1.GND, RE2.GND
  3.3V: Mod1.pin_39, Part1.3.3V, RE2.Vcc

custom parts:
  Raspberry Pi Pico: Raspberry Pi Pico. Based around the RP2040 microcontroller the Pico is a low cost microcontroller device bringing Raspberry Pi quality, cost, and easy of use to the microcontroller space. Jan 2021, Split part in to two versions: tht (this one) and SMD. This one will drill holes for a .1 in header in pcb to allow plugging in the module as well as providing pads to solder the module to the top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
  TFT 2.8 inch 320x240 Touch w microSD: This TFT display is big (2.8" diagonal) bright (4 white-LED backlight) and colorful! 240x320 pixels with individual RGB pixel control. As a bonus, this display has a resistive touchscreen attached to it already, so you can detect finger presses anywhere on the screen.
  KY-040 Rotary encoder: KY-040 Rotary Encoder with switch on breakout borad from AZ Delivery
